// Logisim project Journey1.circ as structural Verilog: 1 circuit, main circuit main
module main (
  output [3:0] High,
  output [3:0] Low,
  output LDA,
  output ADD,
  output SUB,
  output OUT,
  output HLT
);

  wire C32_2_out, C32_out, C33_2_out, C33_out, C34_out, not_1_out, not_2_out, not_3_out, not_4_out;
  wire [3:0] Counter_q, MAR_q;
  wire [7:0] Inst_Reg_q, ram_1_data;

  Counter #(.width(4), .max('hf), .trigger("falling")) Counter (.Q(Counter_q));  // open: load, D, count, carry, clk, clr
  Register #(.width(4)) MAR (.D(Counter_q), .Q(MAR_q));  // open: en, clk, clr
  Register Inst_Reg (.D(ram_1_data), .Q(Inst_Reg_q));  // open: en, clk, clr
  RAM #(.addrWidth(4)) ram_1 (.addr(MAR_q), .data(ram_1_data));  // open: sel, clk, ld, clr
  not not_1 (not_1_out, Inst_Reg_q[7]);
  not not_2 (not_2_out, Inst_Reg_q[6]);
  not not_3 (not_3_out, Inst_Reg_q[5]);
  not not_4 (not_4_out, Inst_Reg_q[4]);
  and C32 (C32_out, not_1_out, not_2_out, not_3_out, not_4_out);
  and C32_2 (C32_2_out, not_1_out, not_2_out, not_3_out, Inst_Reg_q[4]);
  and C33 (C33_out, not_1_out, not_2_out, Inst_Reg_q[5], not_4_out);
  and C33_2 (C33_2_out, Inst_Reg_q[7], Inst_Reg_q[6], Inst_Reg_q[5], not_4_out);
  and C34 (C34_out, Inst_Reg_q[7], Inst_Reg_q[6], Inst_Reg_q[5], Inst_Reg_q[4]);
  buf buffer_1 (LDA, C32_out);
  buf buffer_2 (ADD, C32_2_out);
  buf buffer_3 (SUB, C33_out);
  buf buffer_4 (OUT, C33_2_out);
  buf buffer_5 (HLT, C34_out);

  // Notes on the sheet:
  //   RAM
  //   i7    i6   i5   i4
endmodule
