// Logisim project Journey2.circ as structural Verilog: 1 circuit, main circuit main
module main (
  input  CLK,
  input  CLR,
  output [3:0] High,
  output [3:0] Low,
  output Ep,
  output Cp,
  output Halt,
  output nLm,
  output nCE,
  output nEl,
  output nLa,
  output Ea,
  output Eu,
  output nLb,
  output nLl,
  output Su,
  output nLo
);

  wire ADD_out, C32_2_out, C32_out, C33_2_out, C33_out, C34_out, LDA_out, nor_1_out, not_1_out, not_2_out,
       not_3_out, not_4_out, not_5_out, or_1_out, or_2_out, or_3_out, or_4_out, or_6_out, OUT_out,
       shift_register_1_q2, shift_register_1_q3, shift_register_1_q4, shift_register_1_q5, SUB_out, undriven,
       undriven_2, undriven_3, undriven_4, undriven_5, undriven_6, undriven_7, undriven_8, undriven_9,
       undriven_10, undriven_11, undriven_12, undriven_13, undriven_14, undriven_15, undriven_16, undriven_17;
  wire [3:0] Counter_q, MAR_q;
  wire [7:0] Inst_Reg_q, ram_1_data;

  Counter #(.width(4), .max('hf), .trigger("falling")) Counter (.Q(Counter_q));  // open: load, D, count, carry, clk, clr
  Register #(.width(4)) MAR (.D(Counter_q), .Q(MAR_q));  // open: en, clk, clr
  Register Inst_Reg (.D(ram_1_data), .Q(Inst_Reg_q));  // open: en, clk, clr
  RAM #(.addrWidth(4)) ram_1 (.addr(MAR_q), .data(ram_1_data));  // open: sel, clk, ld, clr
  not not_1 (not_1_out, Inst_Reg_q[7]);
  not not_2 (not_2_out, Inst_Reg_q[6]);
  not not_3 (not_3_out, Inst_Reg_q[5]);
  not not_4 (not_4_out, Inst_Reg_q[4]);
  and C32 (C32_out, not_1_out, not_2_out, not_3_out, not_4_out);
  and C32_2 (C32_2_out, not_1_out, not_2_out, not_3_out, Inst_Reg_q[4]);
  and C33 (C33_out, not_1_out, not_2_out, Inst_Reg_q[5], not_4_out);
  and C33_2 (C33_2_out, Inst_Reg_q[7], Inst_Reg_q[6], Inst_Reg_q[5], not_4_out);
  and C34 (C34_out, Inst_Reg_q[7], Inst_Reg_q[6], Inst_Reg_q[5], Inst_Reg_q[4]);
  // AND_Gate C39 is placed but not wired
  // AND_Gate C39_2 is placed but not wired
  // AND_Gate C39_3 is placed but not wired
  buf LDA (LDA_out, C32_out);
  buf ADD (ADD_out, C32_2_out);
  buf SUB (SUB_out, C33_out);
  buf OUT (OUT_out, C33_2_out);
  buf u_HALT (Halt, C34_out);
  // AND_Gate C39_4 is placed but not wired
  // AND_Gate C39_5 is placed but not wired
  // AND_Gate C39_6 is placed but not wired
  // AND_Gate C39_7 is placed but not wired
  // AND_Gate C39_8 is placed but not wired
  not not_5 (not_5_out, CLK);
  or or_1 (or_1_out, shift_register_1_q2, undriven_4, undriven_5, undriven_6);
  or or_2 (or_2_out, Ep, undriven, undriven_2, undriven_3);
  not not_6 (nLm, or_2_out);
  not not_7 (nCE, or_1_out);
  Shift_Register #(.length(6)) shift_register_1 (
    .in(nor_1_out), .clk(not_5_out), .clr(CLR), .q0(Ep), .q1(Cp), .q2(shift_register_1_q2),
    .q3(shift_register_1_q3), .q4(shift_register_1_q4), .q5(shift_register_1_q5));  // open: shift, out, load, d0, d1, d2, d3, d4, d5
  or or_3 (or_3_out, undriven_7, undriven_8, undriven_9);
  not not_8 (nEl, or_3_out);
  or or_4 (or_4_out, undriven_10, undriven_11, undriven_12);
  not not_9 (nLa, or_4_out);
  or or_5 (Eu, undriven_13, undriven_14);
  nor nor_1 (nor_1_out, Ep, Cp, shift_register_1_q2, shift_register_1_q3, shift_register_1_q4);
  or or_6 (or_6_out, undriven_15, undriven_16);
  not not_10 (nLb, or_6_out);
  not not_11 (nLo, undriven_17);
  not not_12 (nLl, shift_register_1_q2);

  // Notes on the sheet:
  //   RAM
  //   i7    i6   i5   i4
endmodule
