// Logisim project Journey3.circ as structural Verilog: 1 circuit, main circuit main
module main (
  input  CLK,
  input  CLR,
  output [3:0] High,
  output [3:0] Low,
  output Ep,
  output Cp,
  output nLl,
  output Eu,
  output nLo,
  output nLb,
  output nLm,
  output nCE,
  output nEl,
  output nLa,
  output Ea,
  output Su,
  output Halt
);

  wire ADD_out, C32_2_out, C32_out, C33_2_out, C33_out, C34_out, C39_2_out, C39_3_out, C39_4_out, C39_out,
       C40_2_out, C40_3_out, C40_4_out, C40_out, C41_2_out, C41_3_out, C41_5_out, C41_6_out, C41_8_out,
       C41_out, C43_2_out, C43_3_out, C43_out, CE_out, EI_out, LA_out, LB_out, LDA_out, LM_out, nor_1_out,
       not_1_out, not_2_out, not_3_out, not_4_out, not_7_out, OUT_out, shift_register_1_q2,
       shift_register_1_q3, shift_register_1_q4, shift_register_1_q5, SUB_out;
  wire [3:0] Counter_q, MAR_q;
  wire [7:0] Inst_Reg_q, ram_1_data;

  Counter #(.width(4), .max('hf), .trigger("falling")) Counter (.Q(Counter_q));  // open: load, D, count, carry, clk, clr
  Register #(.width(4)) MAR (.D(Counter_q), .Q(MAR_q));  // open: en, clk, clr
  Register Inst_Reg (.D(ram_1_data), .Q(Inst_Reg_q));  // open: en, clk, clr
  RAM #(.addrWidth(4)) ram_1 (.addr(MAR_q), .data(ram_1_data));  // open: sel, clk, ld, clr
  not not_1 (not_1_out, Inst_Reg_q[7]);
  not not_2 (not_2_out, Inst_Reg_q[6]);
  not not_3 (not_3_out, Inst_Reg_q[5]);
  not not_4 (not_4_out, Inst_Reg_q[4]);
  and C32 (C32_out, not_1_out, not_2_out, not_3_out, not_4_out);
  and C32_2 (C32_2_out, not_1_out, not_2_out, not_3_out, Inst_Reg_q[4]);
  and C33 (C33_out, not_1_out, not_2_out, Inst_Reg_q[5], not_4_out);
  and C33_2 (C33_2_out, Inst_Reg_q[7], Inst_Reg_q[6], Inst_Reg_q[5], not_4_out);
  and C34 (C34_out, Inst_Reg_q[7], Inst_Reg_q[6], Inst_Reg_q[5], Inst_Reg_q[4]);
  buf LDA (LDA_out, C32_out);
  buf ADD (ADD_out, C32_2_out);
  buf SUB (SUB_out, C33_out);
  buf OUT (OUT_out, C33_2_out);
  buf u_HALT (Halt, C34_out);
  and C39 (C39_out, ADD_out, shift_register_1_q3);
  and C39_2 (C39_2_out, LDA_out, shift_register_1_q3);
  or LM (LM_out, Ep, C39_2_out, C39_out, C39_3_out);
  not not_5 (nLm, LM_out);
  and C39_3 (C39_3_out, SUB_out, shift_register_1_q3);
  and C40 (C40_out, ADD_out, shift_register_1_q4);
  and C39_4 (C39_4_out, LDA_out, shift_register_1_q4);
  and C40_2 (C40_2_out, LDA_out, shift_register_1_q3);
  and C40_3 (C40_3_out, SUB_out, shift_register_1_q4);
  or CE (CE_out, shift_register_1_q2, C39_4_out, C40_out, C40_3_out);
  not not_6 (nCE, CE_out);
  not not_7 (not_7_out, CLK);
  and C40_4 (C40_4_out, ADD_out, shift_register_1_q3);
  Shift_Register #(.length(6)) shift_register_1 (
    .in(nor_1_out), .clk(not_7_out), .clr(CLR), .q0(Ep), .q1(Cp), .q2(shift_register_1_q2),
    .q3(shift_register_1_q3), .q4(shift_register_1_q4), .q5(shift_register_1_q5));  // open: shift, out, load, d0, d1, d2, d3, d4, d5
  and C41 (C41_out, SUB_out, shift_register_1_q3);
  and C41_2 (C41_2_out, ADD_out, shift_register_1_q5);
  and C41_3 (C41_3_out, LDA_out, shift_register_1_q4);
  or LA (LA_out, C41_3_out, C41_2_out, C41_5_out);
  or EI (EI_out, C40_2_out, C40_4_out, C41_out);
  not not_8 (nEl, EI_out);
  not not_9 (nLa, LA_out);
  and C41_4 (Ea, OUT_out, shift_register_1_q3);
  and C41_5 (C41_5_out, SUB_out, shift_register_1_q5);
  and C41_6 (C41_6_out, ADD_out, shift_register_1_q5);
  and C41_7 (Su, SUB_out, shift_register_1_q5);
  or u_EU (Eu, C41_6_out, C41_8_out);
  nor nor_1 (nor_1_out, Ep, Cp, shift_register_1_q2, shift_register_1_q3, shift_register_1_q4);
  and C41_8 (C41_8_out, SUB_out, shift_register_1_q5);
  and C43 (C43_out, ADD_out, shift_register_1_q4);
  and C43_2 (C43_2_out, SUB_out, shift_register_1_q4);
  and C43_3 (C43_3_out, OUT_out, shift_register_1_q3);
  or LB (LB_out, C43_out, C43_2_out);
  not not_10 (nLb, LB_out);
  not LO (nLo, C43_3_out);
  not not_11 (nLl, shift_register_1_q2);

  // Notes on the sheet:
  //   RAM
  //   i7    i6   i5   i4
endmodule
