// Logisim project Journey6.circ as structural Verilog: 1 circuit, main circuit main
module main (
  input  CLR,
  output [3:0] High,
  output [3:0] Low,
  output out_4,
  output out_5,
  output out_6,
  output out_7,
  output out_8,
  output out_9,
  output out_10,
  output out_11,
  output CLK,
  output Ep,
  output Cp,
  output nLm,
  output nCE,
  output nEl,
  output nLa,
  output Ea,
  output Su,
  output Eu,
  output nLb,
  output nLo,
  output nLl,
  output Halt
);

  wire ADD_out, C32_2_out, C32_out, C33_2_out, C33_out, C34_out, C39_2_out, C39_3_out, C39_4_out, C39_out,
       C40_2_out, C40_3_out, C40_4_out, C40_out, C41_2_out, C41_3_out, C41_4_out, C41_6_out, C41_8_out,
       C41_out, C43_2_out, C43_3_out, C43_out, CE_out, clock_1_out, controlled_buffer_1_out, EI_out, LA_out,
       LB_out, LDA_out, LM_out, nor_1_out, not_1_out, not_2_out, not_3_out, not_4_out, not_5_out, not_6_out,
       not_7_out, not_8_out, not_10_out, not_11_out, not_12_out, not_14_out, not_15_out, not_16_out, OUT_out,
       shift_register_1_q2, shift_register_1_q3, shift_register_1_q4, shift_register_1_q5, SUB_out;
  wire [3:0] Counter_q, MAR_q;
  wire [7:0] adder_1_out, controlled_buffer_6_out, Inst_Reg_q, Reg_A_q, Reg_B_q;

  assign controlled_buffer_1_out = Cp ? CLK : 1'bz;  // Controlled_Buffer controlled_buffer_1
  not not_1 (not_1_out, nLm);
  not not_2 (not_2_out, nCE);
  not not_3 (not_3_out, nLl);
  Counter #(.width(4), .max('hf), .trigger("falling")) Counter (
    .Q(Counter_q), .clk(controlled_buffer_1_out));  // open: load, D, count, carry, clr
  Register #(.width(4)) MAR (.D(Low), .en(not_1_out), .Q(MAR_q), .clk(CLK));  // open: clr
  Register Inst_Reg (.D({High, Low}), .en(not_3_out), .Q(Inst_Reg_q), .clk(CLK));  // open: clr
  RAM #(.addrWidth(4)) ram_1 (.addr(MAR_q), .data({High, Low}), .ld(not_2_out));  // open: sel, clk, clr
  assign Low = Ep ? Counter_q : 4'bz;  // Controlled_Buffer controlled_buffer_2
  not not_4 (not_4_out, Inst_Reg_q[7]);
  not not_5 (not_5_out, Inst_Reg_q[6]);
  not not_6 (not_6_out, Inst_Reg_q[5]);
  not not_7 (not_7_out, Inst_Reg_q[4]);
  and C32 (C32_out, not_4_out, not_5_out, not_6_out, not_7_out);
  and C32_2 (C32_2_out, not_4_out, not_5_out, not_6_out, Inst_Reg_q[4]);
  and C33 (C33_out, not_4_out, not_5_out, Inst_Reg_q[5], not_7_out);
  and C33_2 (C33_2_out, Inst_Reg_q[7], Inst_Reg_q[6], Inst_Reg_q[5], not_7_out);
  and C34 (C34_out, Inst_Reg_q[7], Inst_Reg_q[6], Inst_Reg_q[5], Inst_Reg_q[4]);
  buf LDA (LDA_out, C32_out);
  buf ADD (ADD_out, C32_2_out);
  buf SUB (SUB_out, C33_out);
  buf OUT (OUT_out, C33_2_out);
  buf u_HALT (Halt, C34_out);
  assign Low = not_8_out ? Inst_Reg_q[3:0] : 4'bz;  // Controlled_Buffer controlled_buffer_3
  not not_8 (not_8_out, nEl);
  and C39 (C39_out, ADD_out, shift_register_1_q3);
  and C39_2 (C39_2_out, LDA_out, shift_register_1_q3);
  or LM (LM_out, Ep, C39_2_out, C39_out, C39_4_out);
  not not_9 (nLm, LM_out);
  assign {High, Low} = Ea ? Reg_A_q : 8'bz;  // Controlled_Buffer controlled_buffer_4
  assign {High, Low} = Eu ? adder_1_out : 8'bz;  // Controlled_Buffer controlled_buffer_5
  not not_10 (not_10_out, nLa);
  and C39_3 (C39_3_out, LDA_out, shift_register_1_q4);
  and C39_4 (C39_4_out, SUB_out, shift_register_1_q3);
  and C40 (C40_out, ADD_out, shift_register_1_q4);
  Register Reg_A (.D({High, Low}), .en(not_10_out), .Q(Reg_A_q), .clk(CLK));  // open: clr
  Adder adder_1 (.a(Reg_A_q), .b(controlled_buffer_6_out), .out(adder_1_out), .cin(Su));  // open: cout
  assign controlled_buffer_6_out = not_14_out ? Reg_B_q : 8'bz;  // Controlled_Buffer controlled_buffer_6
  assign controlled_buffer_6_out = Su ? ~Reg_B_q : 8'bz;  // Controlled_Inverter controlled_inverter_1
  Register Reg_B (.D({High, Low}), .en(not_11_out), .Q(Reg_B_q), .clk(CLK));  // open: clr
  not not_11 (not_11_out, nLb);
  Register Output (
    .D({High, Low}), .en(not_12_out), .Q({out_11, out_10, out_9, out_8, out_7, out_6, out_5, out_4}),
    .clk(CLK));  // open: clr
  not not_12 (not_12_out, nLo);
  and C40_2 (C40_2_out, LDA_out, shift_register_1_q3);
  and C40_3 (C40_3_out, SUB_out, shift_register_1_q4);
  or CE (CE_out, shift_register_1_q2, C39_3_out, C40_out, C40_3_out);
  not not_13 (nCE, CE_out);
  not not_14 (not_14_out, Su);
  Clock clock_1 (.out(clock_1_out));
  not not_15 (not_15_out, Halt);
  assign CLK = not_15_out ? clock_1_out : 1'bz;  // Controlled_Buffer controlled_buffer_7
  not not_16 (not_16_out, CLK);
  and C40_4 (C40_4_out, ADD_out, shift_register_1_q3);
  Hex_Digit_Display hex_digit_display_1 (.value({out_7, out_6, out_5, out_4}));  // open: dp
  Hex_Digit_Display hex_digit_display_2 (.value({out_11, out_10, out_9, out_8}));  // open: dp
  Shift_Register #(.length(6)) shift_register_1 (
    .in(nor_1_out), .clk(not_16_out), .clr(CLR), .q0(Ep), .q1(Cp), .q2(shift_register_1_q2),
    .q3(shift_register_1_q3), .q4(shift_register_1_q4), .q5(shift_register_1_q5));  // open: shift, out, load, d0, d1, d2, d3, d4, d5
  and C41 (C41_out, SUB_out, shift_register_1_q3);
  and C41_2 (C41_2_out, ADD_out, shift_register_1_q5);
  and C41_3 (C41_3_out, LDA_out, shift_register_1_q4);
  or LA (LA_out, C41_3_out, C41_2_out, C41_4_out);
  or EI (EI_out, C40_2_out, C40_4_out, C41_out);
  not not_17 (nLa, LA_out);
  not not_18 (nEl, EI_out);
  and C41_4 (C41_4_out, SUB_out, shift_register_1_q5);
  and C41_5 (Ea, OUT_out, shift_register_1_q3);
  and C41_6 (C41_6_out, ADD_out, shift_register_1_q5);
  and C41_7 (Su, SUB_out, shift_register_1_q5);
  or u_EU (Eu, C41_6_out, C41_8_out);
  nor nor_1 (nor_1_out, Ep, Cp, shift_register_1_q2, shift_register_1_q3, shift_register_1_q4);
  and C41_8 (C41_8_out, SUB_out, shift_register_1_q5);
  and C43 (C43_out, ADD_out, shift_register_1_q4);
  and C43_2 (C43_2_out, SUB_out, shift_register_1_q4);
  and C43_3 (C43_3_out, OUT_out, shift_register_1_q3);
  or LB (LB_out, C43_out, C43_2_out);
  not not_19 (nLb, LB_out);
  not LO (nLo, C43_3_out);
  not LI (nLl, shift_register_1_q2);

  // Notes on the sheet:
  //   CLOCK LINE
  //   RAM
  //   i7    i6   i5   i4
  //   ADD/SUB
endmodule
