// Logisim project Module1_ProgramCounter.circ as structural Verilog: 1 circuit, main circuit main
module main (
);

  wire button_1_out, clock_1_out;
  wire [3:0] counter_1_q;
  wire [6:0] rom_1_data;

  Counter #(.width(4), .max('hf), .ongoal("stay")) counter_1 (
    .Q(counter_1_q), .clk(clock_1_out), .clr(button_1_out));  // open: load, D, count, carry
  Clock clock_1 (.out(clock_1_out));
  Counter #(.width(4), .max('hf)) counter_2 ();  // open: load, D, count, Q, carry, clk, clr
  Button button_1 (.out(button_1_out));
  ROM #(.addrWidth(4), .dataWidth(7)) rom_1 (.addr(counter_1_q), .data(rom_1_data));  // open: sel
  TTY tty_1 (.data(rom_1_data), .clk(clock_1_out), .clr(button_1_out));  // open: we

  // Notes on the sheet:
  //   PROGRAM COUNTER
  //   Memory
  //   contents of rom_1 (hex, n*v repeats v):
  //   2d 23 0 4 5 7e 5 5a f e 5f 0 53 0 6d 7e
endmodule
