// Logisim project Module2_MemoryAddressRegister.circ as structural Verilog: 1 circuit, main circuit main
module main (
);

  wire button_1_out, clock_1_out;
  wire [3:0] counter_1_q;

  Counter #(.width(4), .max('hf), .ongoal("stay")) counter_1 (
    .Q(counter_1_q), .clk(clock_1_out), .clr(button_1_out));  // open: load, D, count, carry
  Clock clock_1 (.out(clock_1_out));
  Counter #(.width(4), .max('hf)) counter_2 ();  // open: load, D, count, Q, carry, clk, clr
  Button button_1 (.out(button_1_out));
  ROM #(.addrWidth(4)) rom_1 (.addr(counter_1_q));  // open: data, sel

  // Notes on the sheet:
  //   PROGRAM COUNTER
  //   MAR
  //   Memory
endmodule
