// Logisim project Module3a_InstructionDecoder.circ as structural Verilog: 1 circuit, main circuit main
module main (
  input  l7,
  input  l6,
  input  l5,
  input  l4,
  output LDA,
  output ADD,
  output SUB,
  output OUT,
  output HLT
);

  wire C32_2_out, C32_out, C33_2_out, C33_out, C34_out, not_1_out, not_2_out, not_3_out, not_4_out;

  not not_1 (not_1_out, l7);
  not not_2 (not_2_out, l6);
  not not_3 (not_3_out, l5);
  not not_4 (not_4_out, l4);
  and C32 (C32_out, not_1_out, not_2_out, not_3_out, not_4_out);
  and C32_2 (C32_2_out, not_1_out, not_2_out, not_3_out, l4);
  and C33 (C33_out, not_1_out, not_2_out, l5, not_4_out);
  and C33_2 (C33_2_out, l7, l6, l5, not_4_out);
  and C34 (C34_out, l7, l6, l5, l4);
  buf buffer_1 (LDA, C32_out);
  buf buffer_2 (ADD, C32_2_out);
  buf buffer_3 (SUB, C33_out);
  buf buffer_4 (OUT, C33_2_out);
  buf buffer_5 (HLT, C34_out);

  // Notes on the sheet:
  //   2
  //   4
  //   6
  //   8
  //   1
  //   3
  //   5
  //   9
endmodule
